// Logisim project CPU.circ as structural Verilog: 20 circuits, main circuit main
module main (
);

  wire CLK, cpu_1_f, cpu_1_mwrite, dipswitch_1_sw2;
  wire [13:0] cpu_1_maddr;
  wire [14:0] cpu_1_p_c;
  wire [15:0] cpu_1_mout, cpu_1_x, cpu_1_y, ram_1_dout, rom_1_data;
  wire [15:14] cpu_1_maddr_2;
  wire [15:15] cpu_1_p_c_2;

  ROM #(.addrWidth(15), .dataWidth(16)) rom_1 (.addr(cpu_1_p_c), .data(rom_1_data));
  Clock clock_1 (.out(CLK));
  DipSwitch #(.number(2)) dipswitch_1 (.sw2(dipswitch_1_sw2));  // open: sw1
  CPU cpu_1 (
    .ins(rom_1_data), .mIN(ram_1_dout), .CLK(CLK), .reset(dipswitch_1_sw2), .mOUT(cpu_1_mout),
    .mWRITE(cpu_1_mwrite), .mADDR({cpu_1_maddr_2, cpu_1_maddr}), .P_C({cpu_1_p_c_2[15], cpu_1_p_c}),
    .f(cpu_1_f), .x(cpu_1_x), .y(cpu_1_y));
  LED led_1 (.in(cpu_1_mwrite));
  LED led_2 (.in(cpu_1_f));
  RAM #(.addrWidth(14), .dataWidth(16), .enables("line")) ram_1 (
    .addr(cpu_1_maddr), .we(cpu_1_mwrite), .clk(CLK), .din(cpu_1_mout), .dout(ram_1_dout));
  // LedBar #(.inputtype("row"), .matrixcols(16)) ledbar_1: pin names not known; wires that end beside it: cpu_1_mout
  // LedBar #(.inputtype("row"), .matrixcols(16)) ledbar_2: pin names not known; wires that end beside it: {cpu_1_maddr_2, cpu_1_maddr}
  // LedBar #(.inputtype("row"), .matrixcols(16)) ledbar_3: pin names not known; wires that end beside it: {cpu_1_p_c_2[15], cpu_1_p_c}
  // LedBar #(.inputtype("row"), .matrixcols(16)) ledbar_4: pin names not known; wires that end beside it: cpu_1_x
  // LedBar #(.inputtype("row"), .matrixcols(16)) ledbar_5: pin names not known; wires that end beside it: cpu_1_y

  // Notes on the sheet:
  //   contents of rom_1 (hex, n*v repeats v):
  //   0 2 ec10 3 e090 0 e308
  //   data out to RAM
  //   address out to RAM
  //   program counter
  //   ALU x Input
  //   ALU y Input
endmodule

module CPU (
  input  [15:0] ins,
  input  [15:0] mIN,
  input  CLK,
  input  reset,
  output [15:0] mOUT,
  output mWRITE,
  output [15:0] mADDR,
  output [15:0] P_C,
  output f,
  output [15:0] x,
  output [15:0] y
);

  wire aluammuxctl_1_out_2, aregloadctl_1_out_2, aregmuxctl_1_o, dregloadctl_1_out_2, ng, pcincctl_1_o,
       pcloadctl_1_o, zr;
  wire [15:0] multiplexer_1_out;

  ARegMuxCtl aregmuxctl_1 (.insIN(ins), .o(aregmuxctl_1_o));
  PCLoadCtl pcloadctl_1 (.ins(ins), .zr(zr), .ng(ng), .o(pcloadctl_1_o));
  ARegLoadCtl aregloadctl_1 (.insIN(ins), .out_2(aregloadctl_1_out_2));
  Multiplexer #(.width(16)) multiplexer_1 (.in0(ins), .in1(mOUT), .out(multiplexer_1_out), .sel(aregmuxctl_1_o));
  DRegLoadCtl dregloadctl_1 (.insIN(ins), .out_2(dregloadctl_1_out_2));
  PCIncCtl pcincctl_1 (.reset(reset), .pcload(pcloadctl_1_o), .o(pcincctl_1_o));
  REG16 A (.load(aregloadctl_1_out_2), .CLK(CLK), .D(multiplexer_1_out), .Q(mADDR));
  REG16 D (.load(dregloadctl_1_out_2), .CLK(CLK), .D(mOUT), .Q(x));
  PC pc_1 (.inc(pcincctl_1_o), .load(pcloadctl_1_o), .reset(reset), .CLK(CLK), .i(mADDR), .o(P_C));
  Multiplexer #(.width(16)) multiplexer_2 (.in0(mADDR), .in1(mIN), .out(y), .sel(aluammuxctl_1_out_2));
  ALUAMMuxCtl aluammuxctl_1 (.insIN(ins), .out_2(aluammuxctl_1_out_2));
  WriteMCtl writemctl_1 (.ins(ins), .o(mWRITE));
  ALU alu_1 (
    .x(x), .zx(ins[11]), .nx(ins[10]), .f(ins[7]), .y(y), .zy(ins[9]), .ny(ins[8]), .no(ins[6]), .o(mOUT),
    .zr(zr), .ng(ng));

  assign f = ins[7];

  // Other names for the same wires on the sheet: aOUT[15:0] = mADDR
endmodule

module HalfAdder (
  input  a,
  input  b,
  output SUM,
  output CARRY
);

  xor xor_1 (SUM, a, b);
  and and_1 (CARRY, a, b);
endmodule

module FullAdder (
  input  a,
  input  b,
  input  cIN,
  output SUM,
  output CARRY
);

  wire halfadder_1_carry, halfadder_1_sum, halfadder_2_carry;

  HalfAdder halfadder_1 (.a(a), .b(b), .SUM(halfadder_1_sum), .CARRY(halfadder_1_carry));
  HalfAdder halfadder_2 (.a(halfadder_1_sum), .b(cIN), .SUM(SUM), .CARRY(halfadder_2_carry));
  or or_1 (CARRY, halfadder_1_carry, halfadder_2_carry);
endmodule

module ADD16 (
  input  [15:0] a,
  input  [15:0] b,
  output [15:0] o
);

  wire fulladder_1_carry, fulladder_2_carry, fulladder_3_carry, fulladder_4_carry, fulladder_5_carry,
       fulladder_6_carry, fulladder_7_carry, fulladder_8_carry, fulladder_9_carry, fulladder_10_carry,
       fulladder_11_carry, fulladder_12_carry, fulladder_13_carry, fulladder_14_carry, fulladder_15_carry;

  FullAdder fulladder_1 (.a(a[0]), .b(b[0]), .SUM(o[0]), .CARRY(fulladder_1_carry));  // open: cIN
  FullAdder fulladder_2 (.a(a[1]), .b(b[1]), .cIN(fulladder_1_carry), .SUM(o[1]), .CARRY(fulladder_2_carry));
  FullAdder fulladder_3 (.a(a[2]), .b(b[2]), .cIN(fulladder_2_carry), .SUM(o[2]), .CARRY(fulladder_3_carry));
  FullAdder fulladder_4 (.a(a[3]), .b(b[3]), .cIN(fulladder_3_carry), .SUM(o[3]), .CARRY(fulladder_4_carry));
  FullAdder fulladder_5 (.a(a[4]), .b(b[4]), .cIN(fulladder_4_carry), .SUM(o[4]), .CARRY(fulladder_5_carry));
  FullAdder fulladder_6 (.a(a[5]), .b(b[5]), .cIN(fulladder_5_carry), .SUM(o[5]), .CARRY(fulladder_6_carry));
  FullAdder fulladder_7 (.a(a[6]), .b(b[6]), .cIN(fulladder_6_carry), .SUM(o[6]), .CARRY(fulladder_7_carry));
  FullAdder fulladder_8 (.a(a[7]), .b(b[7]), .cIN(fulladder_7_carry), .SUM(o[7]), .CARRY(fulladder_8_carry));
  FullAdder fulladder_9 (.a(a[8]), .b(b[8]), .cIN(fulladder_8_carry), .SUM(o[8]), .CARRY(fulladder_9_carry));
  FullAdder fulladder_10 (.a(a[9]), .b(b[9]), .cIN(fulladder_9_carry), .SUM(o[9]), .CARRY(fulladder_10_carry));
  FullAdder fulladder_11 (.a(a[10]), .b(b[10]), .cIN(fulladder_10_carry), .SUM(o[10]), .CARRY(fulladder_11_carry));
  FullAdder fulladder_12 (.a(a[11]), .b(b[11]), .cIN(fulladder_11_carry), .SUM(o[11]), .CARRY(fulladder_12_carry));
  FullAdder fulladder_13 (.a(a[12]), .b(b[12]), .cIN(fulladder_12_carry), .SUM(o[12]), .CARRY(fulladder_13_carry));
  FullAdder fulladder_14 (.a(a[13]), .b(b[13]), .cIN(fulladder_13_carry), .SUM(o[13]), .CARRY(fulladder_14_carry));
  FullAdder fulladder_15 (.a(a[14]), .b(b[14]), .cIN(fulladder_14_carry), .SUM(o[14]), .CARRY(fulladder_15_carry));
  FullAdder fulladder_16 (.a(a[15]), .b(b[15]), .cIN(fulladder_15_carry), .SUM(o[15]));  // open: CARRY
endmodule

module INC16 (
  input  [15:0] a,
  output [15:0] o
);

  ADD16 add16_1 (.a(a), .b(16'h1), .o(o));
endmodule

module ALU (
  input  [15:0] x,
  input  zx,
  input  nx,
  input  f,
  input  [15:0] y,
  input  zy,
  input  ny,
  input  no,
  output [15:0] o,
  output zr,
  output ng
);

  wire or_1_out;
  wire [15:0] add16_1_o, and_1_out, multiplexer_1_out, multiplexer_2_out, multiplexer_3_out,
       multiplexer_4_out, multiplexer_6_out, not_1_out, not_2_out, not_3_out;

  Multiplexer #(.width(16)) multiplexer_1 (.in0(x), .in1({16{1'b0}}), .out(multiplexer_1_out), .sel(zx));
  Multiplexer #(.width(16)) multiplexer_2 (.in0(y), .in1({16{1'b0}}), .out(multiplexer_2_out), .sel(zy));
  assign not_1_out = ~multiplexer_6_out;  // NOT_Gate not_1, 16 bits wide
  Multiplexer #(.width(16)) multiplexer_3 (.in0(multiplexer_1_out), .in1(not_2_out), .out(multiplexer_3_out), .sel(nx));
  assign not_2_out = ~multiplexer_1_out;  // NOT_Gate not_2, 16 bits wide
  Multiplexer #(.width(16)) multiplexer_4 (.in0(multiplexer_2_out), .in1(not_3_out), .out(multiplexer_4_out), .sel(ny));
  assign not_3_out = ~multiplexer_2_out;  // NOT_Gate not_3, 16 bits wide
  Multiplexer #(.width(16)) multiplexer_5 (.in0(multiplexer_6_out), .in1(not_1_out), .out({ng, o[14:0]}), .sel(no));
  assign and_1_out = multiplexer_3_out & multiplexer_4_out;  // AND_Gate and_1, 16 bits wide
  ADD16 add16_1 (.a(multiplexer_3_out), .b(multiplexer_4_out), .o(add16_1_o));
  Multiplexer #(.width(16)) multiplexer_6 (.in0(and_1_out), .in1(add16_1_o), .out(multiplexer_6_out), .sel(f));
  or or_1 (or_1_out, o[0], o[1], o[2], o[3], o[4], o[5], o[6], o[7], o[8], o[9], o[10], o[11], o[12], o[13], o[14], ng);
  not not_4 (zr, or_1_out);

  assign o[15] = ng;
endmodule

module ALU_Test (
);

  wire alu_1_ng, alu_1_zr, flags_sw1, flags_sw2, flags_sw3, flags_sw4, flags_sw5, flags_sw6;
  wire [7:0] dipswitch_1_sw8;
  wire [15:0] o_p1, undriven;

  DipSwitch dipswitch_1 (
    .sw1(dipswitch_1_sw8[7]), .sw2(dipswitch_1_sw8[6]), .sw3(dipswitch_1_sw8[5]), .sw4(dipswitch_1_sw8[4]),
    .sw5(dipswitch_1_sw8[3]), .sw6(dipswitch_1_sw8[2]), .sw7(dipswitch_1_sw8[1]), .sw8(dipswitch_1_sw8[0]));
  // DipSwitch #(.number(16)) dipswitch_2: pin names not known
  DipSwitch flags (
    .sw1(flags_sw1), .sw2(flags_sw2), .sw3(flags_sw3), .sw4(flags_sw4), .sw5(flags_sw5), .sw6(flags_sw6));  // open: sw7, sw8
  // LedBar #(.inputtype("row"), .matrixcols(16)) o: pin names not known; wires that end beside it: o_p1
  ALU alu_1 (
    .x(undriven), .zx(flags_sw1), .nx(flags_sw2), .f(flags_sw3), .y({{8{1'b0}}, dipswitch_1_sw8}),
    .zy(flags_sw4), .ny(flags_sw5), .no(flags_sw6), .o(o_p1), .zr(alu_1_zr), .ng(alu_1_ng));
  LED zero (.in(alu_1_zr));
  LED negative (.in(alu_1_ng));
endmodule

module Bit (
  input  i,
  input  load,
  input  CLK,
  output o
);

  wire multiplexer_1_out;

  D_Flip_Flop d_ff_1 (.D(multiplexer_1_out), .clk(CLK), .Q(o), .preset(1'b0), .reset(1'b0));  // open: Qn
  Multiplexer multiplexer_1 (.in0(o), .in1(i), .out(multiplexer_1_out), .sel(load));
endmodule

module REG16 (
  input  load,
  input  CLK,
  input  [15:0] D,
  output [15:0] Q
);

  Bit bit_1 (.i(D[0]), .load(load), .CLK(CLK), .o(Q[0]));
  Bit bit_2 (.i(D[1]), .load(load), .CLK(CLK), .o(Q[1]));
  Bit bit_3 (.i(D[2]), .load(load), .CLK(CLK), .o(Q[2]));
  Bit bit_4 (.i(D[3]), .load(load), .CLK(CLK), .o(Q[3]));
  Bit bit_5 (.i(D[4]), .load(load), .CLK(CLK), .o(Q[4]));
  Bit bit_6 (.i(D[5]), .load(load), .CLK(CLK), .o(Q[5]));
  Bit bit_7 (.i(D[6]), .load(load), .CLK(CLK), .o(Q[6]));
  Bit bit_8 (.i(D[7]), .load(load), .CLK(CLK), .o(Q[7]));
  Bit bit_9 (.i(D[8]), .load(load), .CLK(CLK), .o(Q[8]));
  Bit bit_10 (.i(D[9]), .load(load), .CLK(CLK), .o(Q[9]));
  Bit bit_11 (.i(D[10]), .load(load), .CLK(CLK), .o(Q[10]));
  Bit bit_12 (.i(D[11]), .load(load), .CLK(CLK), .o(Q[11]));
  Bit bit_13 (.i(D[12]), .load(load), .CLK(CLK), .o(Q[12]));
  Bit bit_14 (.i(D[13]), .load(load), .CLK(CLK), .o(Q[13]));
  Bit bit_15 (.i(D[14]), .load(load), .CLK(CLK), .o(Q[14]));
  Bit bit_16 (.i(D[15]), .load(load), .CLK(CLK), .o(Q[15]));
endmodule

module RAM16K_FULL (
  input  load,
  input  CLK,
  input  [15:0] dIN,
  input  [13:0] aIN,
  output [15:0] dOUT
);

  RAM #(.addrWidth(14), .dataWidth(16), .enables("line")) ram_1 (
    .addr(aIN), .we(load), .clk(CLK), .din(dIN), .dout(dOUT));
endmodule

module PC (
  input  inc,
  input  load,
  input  reset,
  input  CLK,
  input  [15:0] i,
  output [15:0] o
);

  wire or_1_out;
  wire [15:0] inc16_1_o, multiplexer_1_out, multiplexer_2_out, multiplexer_3_out;

  Multiplexer #(.width(16)) multiplexer_1 (.in1(inc16_1_o), .out(multiplexer_1_out), .sel(inc));  // open: in0
  Multiplexer #(.width(16)) multiplexer_2 (.in0(multiplexer_1_out), .in1(i), .out(multiplexer_2_out), .sel(load));
  or or_1 (or_1_out, inc, load, reset);
  Multiplexer #(.width(16)) multiplexer_3 (
    .in0(multiplexer_2_out), .in1({16{1'b0}}), .out(multiplexer_3_out), .sel(reset));
  REG16 reg16_1 (.load(or_1_out), .CLK(CLK), .D(multiplexer_3_out), .Q(o));
  INC16 inc16_1 (.a(o), .o(inc16_1_o));
endmodule

module PC_Test (
);

  wire clock_1_out, dipswitch_2_p1, dipswitch_2_p2, dipswitch_2_p3;
  wire [15:0] dipswitch_1_sw16, pc_1_o;

  DipSwitch #(.number(16)) dipswitch_1 (
    .sw1(dipswitch_1_sw16[15]), .sw2(dipswitch_1_sw16[14]), .sw3(dipswitch_1_sw16[13]),
    .sw4(dipswitch_1_sw16[12]), .sw5(dipswitch_1_sw16[11]), .sw6(dipswitch_1_sw16[10]),
    .sw7(dipswitch_1_sw16[9]), .sw8(dipswitch_1_sw16[8]), .sw9(dipswitch_1_sw16[7]),
    .sw10(dipswitch_1_sw16[6]), .sw11(dipswitch_1_sw16[5]), .sw12(dipswitch_1_sw16[4]),
    .sw13(dipswitch_1_sw16[3]), .sw14(dipswitch_1_sw16[2]), .sw15(dipswitch_1_sw16[1]),
    .sw16(dipswitch_1_sw16[0]));
  // DipSwitch #(.number(3)) dipswitch_2: pin names not known; wires that end beside it: dipswitch_2_p1, dipswitch_2_p2, dipswitch_2_p3
  Clock clock_1 (.out(clock_1_out));
  PC pc_1 (
    .inc(dipswitch_2_p1), .load(dipswitch_2_p2), .reset(dipswitch_2_p3), .CLK(clock_1_out),
    .i(dipswitch_1_sw16), .o(pc_1_o));
  LED led_1 (.in(pc_1_o[15]));
  LED led_2 (.in(pc_1_o[14]));
  LED led_3 (.in(pc_1_o[13]));
  LED led_4 (.in(pc_1_o[12]));
  LED led_5 (.in(pc_1_o[11]));
  LED led_6 (.in(pc_1_o[10]));
  LED led_7 (.in(pc_1_o[9]));
  LED led_8 (.in(pc_1_o[8]));
  LED led_9 (.in(pc_1_o[7]));
  LED led_10 (.in(pc_1_o[6]));
  LED led_11 (.in(pc_1_o[5]));
  LED led_12 (.in(pc_1_o[4]));
  LED led_13 (.in(pc_1_o[3]));
  LED led_14 (.in(pc_1_o[2]));
  LED led_15 (.in(pc_1_o[1]));
  LED led_16 (.in(pc_1_o[0]));
endmodule

module ARegMuxCtl (
  input  [15:0] insIN,
  output o
);

  // NoConnect on insIN[0]
  // NoConnect on insIN[1]
  // NoConnect on insIN[2]
  // NoConnect on insIN[3]
  // NoConnect on insIN[4]
  // NoConnect on insIN[5]
  // NoConnect on insIN[6]
  // NoConnect on insIN[7]
  // NoConnect on insIN[8]
  // NoConnect on insIN[9]
  // NoConnect on insIN[10]
  // NoConnect on insIN[11]
  // NoConnect on insIN[12]
  // NoConnect on insIN[13]
  // NoConnect on insIN[14]

  assign o = insIN[15];
endmodule

module ARegLoadCtl (
  input  [15:0] insIN,
  output out_2
);

  wire and_1_out, not_1_out;

  and and_1 (and_1_out, insIN[5], insIN[15]);
  not not_1 (not_1_out, insIN[15]);
  or or_1 (out_2, and_1_out, not_1_out);
endmodule

module ALUAMMuxCtl (
  input  [15:0] insIN,
  output out_2
);

  and and_1 (out_2, insIN[12], insIN[15]);

  // Notes on the sheet:
  //   i AND a
endmodule

module DRegLoadCtl (
  input  [15:0] insIN,
  output out_2
);

  and and_1 (out_2, insIN[4], insIN[15]);
endmodule

module WriteMCtl (
  input  [15:0] ins,
  output o
);

  and and_1 (o, ins[3], ins[15]);
endmodule

module PCLoadCtl (
  input  [15:0] ins,
  input  zr,
  input  ng,
  output o
);

  wire jeq_out, jge_out, jgt_out, jle_out, jlt_out, jmp_out, jne_out, notj1, notj2, notj3, notng, notzr,
       or_1_out, or_2_out, or_3_out;

  not not_1 (notzr, zr);
  not not_2 (notng, ng);
  not not_3 (notj3, ins[0]);
  not not_4 (notj2, ins[1]);
  not not_5 (notj1, ins[2]);
  or or_1 (or_1_out, zr, notng);
  and jgt (jgt_out, notj1, notj2, ins[0], notzr, notng);
  and jeq (jeq_out, notj1, ins[1], notj3, zr);
  and jge (jge_out, notj1, ins[1], ins[0], or_1_out);
  and jlt (jlt_out, ins[2], notj2, notj3, notzr, ng);
  or or_2 (or_2_out, zr, ng);
  and jne (jne_out, ins[2], notj2, ins[0], notzr);
  and jle (jle_out, ins[2], ins[1], notj3, or_2_out);
  and jmp (jmp_out, ins[2], ins[1], ins[0]);
  or or_3 (or_3_out, jgt_out, jne_out, jeq_out, jle_out, jge_out, jmp_out, jlt_out);
  and and_1 (o, or_3_out, ins[15]);

  // Other names for the same wires on the sheet: j3 = ins[0]; j2 = ins[1]; j1 = ins[2]; i = ins[15]
endmodule

module PCIncCtl (
  input  reset,
  input  pcload,
  output o
);

  and and_1 (o, ~reset, ~pcload);  // AND_Gate
endmodule
